# Fritzing sketch MotorShieldExtAlim (saved by Fritzing 0.9.3b)

parts:
  pyboard_v1_1 = PyBoard v1.0
  Composant1 = Adafruit Motor/Stepper/Servo Shield [part_number="Adafruit #1438"]
  M1 = Stepper Motor - Bipolar
  M2 = DC Motor
  Power_plug1 = Power plug
  J1 = Basic Servo

nets:
  N1: pyboard_v1_1.X9, Composant1.AD5/SCL
  N2: pyboard_v1_1.X10, Composant1.AD4/SDA
  GND: pyboard_v1_1.GND, Composant1.GND, Power_plug1.GND, J1.gnd
  VIN: pyboard_v1_1.VIN, Composant1.+5V, J1.vcc
  N3: Composant1.M2A, M1.A
  N4: Composant1.M2B, M1.C
  N5: Composant1.M1B, M1.B
  N6: Composant1.M1A, M1.D
  N7: Composant1.M3A, M2.pin_2
  N8: Composant1.M3B, M2.pin_1
  N9: Composant1.PWM0, J1.pulse
  N10: Composant1.VMOTOR, Power_plug1.VCC

custom parts:
  Adafruit Motor/Stepper/Servo Shield: The original Adafruit Motorshield kit is one of our most beloved kits, which is why we decided to make something even better. We have upgraded the shield kit to make the bestest, easiest way to drive DC and Stepper motors. This shield will make quick work of your next robotics project! We kept the ability to drive up to 4 DC motors or 2 stepper motors, but added many improvements: Instead of a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
