# Fritzing sketch MotorShieldPyboardAlim (saved by Fritzing 0.9.6b)

parts:
  pyboard_v1_1 = PyBoard v1.0
  Composant1 = Adafruit Motor/Stepper/Servo Shield [part_number="Adafruit #1438"]
  M1 = Stepper Motor - Bipolar
  M2 = DC Motor
  J2 = Basic Servo

nets:
  N1: pyboard_v1_1.X9, Composant1.AD5/SCL
  N2: pyboard_v1_1.X10, Composant1.AD4/SDA
  N3: pyboard_v1_1.VIN#41, Composant1.VIN
  GND: pyboard_v1_1.GND, Composant1.GND, J2.gnd
  +5V: pyboard_v1_1.VIN#57, Composant1.+5V, J2.vcc
  N4: Composant1.M2A, M1.A
  N5: Composant1.M2B, M1.C
  N6: Composant1.M1B, M1.B
  N7: Composant1.M1A, M1.D
  N8: Composant1.M3A, M2.pin_2
  N9: Composant1.M3B, M2.pin_1
  N10: Composant1.PWM0, J2.pulse

notes:
  Connect heads of VIN jumper on the shield

custom parts:
  Adafruit Motor/Stepper/Servo Shield: The original Adafruit Motorshield kit is one of our most beloved kits, which is why we decided to make something even better. We have upgraded the shield kit to make the bestest, easiest way to drive DC and Stepper motors. This shield will make quick work of your next robotics project! We kept the ability to drive up to 4 DC motors or 2 stepper motors, but added many improvements: Instead of a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
