# Fritzing sketch ExamplePyboard (saved by Fritzing 0.9.3b)
breadboards: 1

parts:
  T1 = TMP36 Temperature Sensor [package="TO92 [THT]"]
  Composant1 = BME280 Breakout  # not connected
  Composant2 = SRF05 Ultrasonic Rangefinder
  pyboard1 = Micro Python pyboard [part_number=PYBv10b]

nets:
  N1: T1.+Vs, pyboard1.P10A_VIN
  N2: T1.Vout, pyboard1.Y12
  N3: T1.GND, pyboard1.P9A_GND
  N4: Composant2.VCC, pyboard1.Y16_VIN
  N5: Composant2.Trig, pyboard1.X11
  N6: Composant2.Echo, pyboard1.X12
  N7: Composant2.GND, pyboard1.Y14_GND
